// Logisim project 4bit_16bit_adder.circ as structural Verilog: 9 circuits, main circuit main
module main (
  input  [3:0] FourBitA,
  input  [3:0] FourBitB,
  input  Cin,
  input  [15:0] HexA,
  input  [15:0] HexB,
  input  in_6,
  input  [15:0] in_7,
  input  in_8,
  input  [15:0] in_9,
  input  in_10,
  input  BitA,
  input  BitB,
  input  in_13,
  input  [15:0] A,
  input  [15:0] B,
  output [3:0] FourSum,
  output Cout1,
  output [15:0] HexSum,
  output Cout2,
  output [15:0] out_20,
  output out_21,
  output out_22,
  output BitSum,
  output Cout3,
  output [15:0] out_25,
  output out_26
);

  wire half_adder_1_cout, hex_clu_adder_1_pgg;

  four_bit_half_adder four_bit_half_adder_1 (.FourBitA(FourBitA), .FourBitB(FourBitB), .Sum(FourSum), .Cout(Cout1));
  hex_full_adder hex_full_adder_1 (.Cin(Cin), .HexA(HexA), .HexB(HexB), .Sum(HexSum), .Cout(Cout2));
  half_adder half_adder_1 (.A(in_8), .B(in_10), .S(out_22), .Cout(half_adder_1_cout));
  full_adder full_adder_1 (.Cin(half_adder_1_cout), .A(BitA), .B(BitB), .Sum(BitSum), .Cout(Cout3));
  hex_CLU_adder hex_clu_adder_1 (.Cin(in_13), .A(A), .B(B), .S(out_25), .PGG(hex_clu_adder_1_pgg), .GGG(out_26));
  hex_full_adder hex_full_adder_2 (.Cin(in_6), .HexA(in_7), .HexB(in_9), .Sum(out_20), .Cout(out_21));
endmodule

module full_adder (
  input  Cin,
  input  A,
  input  B,
  output Sum,
  output Cout
);

  wire and_1_out, and_2_out, xor_1_out;

  xor xor_1 (xor_1_out, Cin, A);
  xor xor_2 (Sum, xor_1_out, B);
  and and_1 (and_1_out, xor_1_out, B);
  or or_1 (Cout, and_1_out, and_2_out);
  and and_2 (and_2_out, Cin, A);
endmodule

module half_adder (
  input  A,
  input  B,
  output S,
  output Cout
);

  xor xor_1 (S, A, B);
  and and_1 (Cout, A, B);
endmodule

module four_bit_half_adder (
  input  [3:0] FourBitA,
  input  [3:0] FourBitB,
  output [3:0] Sum,
  output Cout
);

  wire full_adder_1_cout, full_adder_2_cout, half_adder_1_cout;

  half_adder half_adder_1 (.A(FourBitA[0]), .B(FourBitB[0]), .S(Sum[0]), .Cout(half_adder_1_cout));
  full_adder full_adder_1 (
    .Cin(half_adder_1_cout), .A(FourBitA[1]), .B(FourBitB[1]), .Sum(Sum[1]), .Cout(full_adder_1_cout));
  full_adder full_adder_2 (
    .Cin(full_adder_1_cout), .A(FourBitA[2]), .B(FourBitB[2]), .Sum(Sum[2]), .Cout(full_adder_2_cout));
  full_adder full_adder_3 (.Cin(full_adder_2_cout), .A(FourBitA[3]), .B(FourBitB[3]), .Sum(Sum[3]), .Cout(Cout));
endmodule

module hex_full_adder (
  input  Cin,
  input  [15:0] HexA,
  input  [15:0] HexB,
  output [15:0] Sum,
  output Cout
);

  wire four_bit_full_adder_1_cout, four_bit_full_adder_2_cout, four_bit_full_adder_3_cout;

  four_bit_full_adder four_bit_full_adder_1 (
    .Cin(Cin), .A(HexA[3:0]), .B(HexB[3:0]), .Sum(Sum[3:0]), .Cout(four_bit_full_adder_1_cout));
  four_bit_full_adder four_bit_full_adder_2 (
    .Cin(four_bit_full_adder_1_cout), .A(HexA[7:4]), .B(HexB[7:4]), .Sum(Sum[7:4]),
    .Cout(four_bit_full_adder_2_cout));
  four_bit_full_adder four_bit_full_adder_3 (
    .Cin(four_bit_full_adder_2_cout), .A(HexA[11:8]), .B(HexB[11:8]), .Sum(Sum[11:8]),
    .Cout(four_bit_full_adder_3_cout));
  four_bit_full_adder four_bit_full_adder_4 (
    .Cin(four_bit_full_adder_3_cout), .A(HexA[15:12]), .B(HexB[15:12]), .Sum(Sum[15:12]), .Cout(Cout));

  // Other names for the same wires on the sheet: A0[3:0] = HexA[3:0]; A1[3:0] = HexA[7:4]; A2[3:0] = HexA[11:8];
  //   A3[3:0] = HexA[15:12]; B0[3:0] = HexB[3:0]; B1[3:0] = HexB[7:4]; B2[3:0] = HexB[11:8]; B3[3:0] = HexB[15:12]

  // Notes on the sheet:
  //   14 ticks
endmodule

module four_bit_full_adder (
  input  Cin,
  input  [3:0] A,
  input  [3:0] B,
  output [3:0] Sum,
  output Cout
);

  wire full_adder_1_cout, full_adder_2_cout, full_adder_3_cout;

  full_adder full_adder_1 (.Cin(Cin), .A(A[0]), .B(B[0]), .Sum(Sum[0]), .Cout(full_adder_1_cout));
  full_adder full_adder_2 (.Cin(full_adder_1_cout), .A(A[1]), .B(B[1]), .Sum(Sum[1]), .Cout(full_adder_2_cout));
  full_adder full_adder_3 (.Cin(full_adder_2_cout), .A(A[2]), .B(B[2]), .Sum(Sum[2]), .Cout(full_adder_3_cout));
  full_adder full_adder_4 (.Cin(full_adder_3_cout), .A(A[3]), .B(B[3]), .Sum(Sum[3]), .Cout(Cout));
endmodule

module CLU (
  input  Cin,
  input  P0,
  input  G0,
  input  P1,
  input  G1,
  input  P2,
  input  G2,
  input  P3,
  input  G3,
  output Cout1,
  output Cout2,
  output Cout3,
  output Cout4,
  output PG,
  output GG
);

  wire and_2_out, and_3_out, and_4_out, and_5_out, and_6_out, and_7_out, and_8_out;

  and and_1 (PG, P0, P1, P2, P3);
  and and_2 (and_2_out, G2, P3);
  and and_3 (and_3_out, G1, P2, G2);
  and and_4 (and_4_out, G0, P1, P2, P3);
  ExactlyOne xor_1 (.out(GG), .in0(and_2_out), .in1(and_3_out), .in2(G3), .in3(and_4_out));
  and and_5 (and_5_out, Cin, P0);
  and and_6 (and_6_out, Cout1, P1);
  and and_7 (and_7_out, Cout2, P2);
  and and_8 (and_8_out, Cout3, P3);
  xor xor_2 (Cout1, and_5_out, G0);
  xor xor_3 (Cout2, and_6_out, G1);
  xor xor_4 (Cout3, and_7_out, G2);
  xor xor_5 (Cout4, and_8_out, G3);
endmodule

module four_bit_CLU_adder (
  input  Cin,
  input  [3:0] A,
  input  [3:0] B,
  output [3:0] S,
  output PG,
  output GG,
  output Cout
);

  wire clu_1_cout1, clu_1_cout2, clu_1_cout3, G0, G1, G2, G3, P0, P1, P2, P3, xor_5_out, xor_6_out,
       xor_7_out, xor_8_out;

  xor xor_1 (P0, A[0], B[0]);
  and and_1 (G0, A[0], B[0]);
  xor xor_2 (P1, A[1], B[1]);
  and and_2 (G1, A[1], B[1]);
  xor xor_3 (P2, A[2], B[2]);
  and and_3 (G2, B[2], A[2]);
  xor xor_4 (P3, A[3], B[3]);
  and and_4 (G3, B[3], A[3]);
  CLU clu_1 (
    .Cin(Cin), .P0(P0), .G0(G0), .P1(P1), .G1(G1), .P2(P2), .G2(G2), .P3(P3), .G3(G3), .Cout1(clu_1_cout1),
    .Cout2(clu_1_cout2), .Cout3(clu_1_cout3), .Cout4(Cout), .PG(PG), .GG(GG));
  xor xor_5 (xor_5_out, clu_1_cout1, A[1]);
  xor xor_6 (xor_6_out, clu_1_cout2, A[2]);
  xor xor_7 (xor_7_out, clu_1_cout3, A[3]);
  xor xor_8 (xor_8_out, Cin, A[0]);
  xor xor_9 (S[0], xor_8_out, B[0]);
  xor xor_10 (S[1], xor_5_out, B[1]);
  xor xor_11 (S[2], xor_6_out, B[2]);
  xor xor_12 (S[3], xor_7_out, B[3]);
endmodule

module hex_CLU_adder (
  input  Cin,
  input  [15:0] A,
  input  [15:0] B,
  output [15:0] S,
  output PGG,
  output GGG
);

  wire four_bit_clu_adder_1_gg, four_bit_clu_adder_1_pg, four_bit_clu_adder_2_gg, four_bit_clu_adder_2_pg,
       four_bit_clu_adder_3_gg, four_bit_clu_adder_3_pg, four_bit_clu_adder_4_gg, four_bit_clu_adder_4_pg,
       O1, O2, O3;

  four_bit_CLU_adder four_bit_clu_adder_1 (
    .Cin(Cin), .A(A[3:0]), .B(B[3:0]), .S(S[3:0]), .PG(four_bit_clu_adder_1_pg), .GG(four_bit_clu_adder_1_gg));  // open: Cout
  four_bit_CLU_adder four_bit_clu_adder_2 (
    .Cin(O1), .A(A[7:4]), .B(B[7:4]), .S(S[7:4]), .PG(four_bit_clu_adder_2_pg), .GG(four_bit_clu_adder_2_gg));  // open: Cout
  four_bit_CLU_adder four_bit_clu_adder_3 (
    .Cin(O2), .A(A[11:8]), .B(B[11:8]), .S(S[11:8]), .PG(four_bit_clu_adder_3_pg),
    .GG(four_bit_clu_adder_3_gg));  // open: Cout
  four_bit_CLU_adder four_bit_clu_adder_4 (
    .Cin(O3), .A(A[15:12]), .B(B[15:12]), .S(S[15:12]), .PG(four_bit_clu_adder_4_pg),
    .GG(four_bit_clu_adder_4_gg));  // open: Cout
  CLU clu_1 (
    .Cin(Cin), .P0(four_bit_clu_adder_1_pg), .G0(four_bit_clu_adder_1_gg), .P1(four_bit_clu_adder_2_pg),
    .G1(four_bit_clu_adder_2_gg), .P2(four_bit_clu_adder_3_pg), .G2(four_bit_clu_adder_3_gg),
    .P3(four_bit_clu_adder_4_pg), .G3(four_bit_clu_adder_4_gg), .Cout1(O1), .Cout2(O2), .Cout3(O3),
    .Cout4(O3), .PG(PGG), .GG(GGG));

  // Other names for the same wires on the sheet: A0[3:0] = A[3:0]; A1[3:0] = A[7:4]; A2[3:0] = A[11:8];
  //   A3[3:0] = A[15:12]; B0[3:0] = B[3:0]; B1[3:0] = B[7:4]; B2[3:0] = B[11:8]; B3[3:0] = B[15:12]; S0[3:0] = S[3:0];
  //   S1[3:0] = S[7:4]; S2[3:0] = S[11:8]; S3[3:0] = S[15:12]
endmodule
