// Logisim project 4bit_mult.circ as structural Verilog: 3 circuits, main circuit main
module main (
  input  [3:0] A,
  input  [3:0] B,
  output [7:0] out_3
);

  wire and_2_out, and_3_out, and_4_out, and_5_out, and_6_out, and_7_out, and_8_out, and_9_out, and_10_out,
       and_11_out, and_12_out, and_13_out, and_14_out, and_15_out, and_16_out, full_adder_1_cout,
       full_adder_1_sum, full_adder_2_cout, full_adder_2_sum, full_adder_3_cout, full_adder_3_sum,
       full_adder_4_cout, full_adder_4_sum, full_adder_5_cout, full_adder_5_sum, full_adder_6_cout,
       full_adder_7_cout, half_adder_1_cout, half_adder_2_cout, half_adder_2_sum, half_adder_3_cout,
       half_adder_4_cout;

  and and_1 (out_3[0], A[0], B[0]);
  and and_2 (and_2_out, A[1], B[0]);
  and and_3 (and_3_out, A[0], B[1]);
  and and_4 (and_4_out, A[2], B[0]);
  and and_5 (and_5_out, A[1], B[1]);
  and and_6 (and_6_out, A[3], B[0]);
  and and_7 (and_7_out, A[2], B[1]);
  and and_8 (and_8_out, A[3], B[1]);
  half_adder half_adder_1 (.A(and_2_out), .B(and_3_out), .Sum(out_3[1]), .Cout(half_adder_1_cout));
  full_adder full_adder_1 (
    .Cin(half_adder_1_cout), .A(and_4_out), .B(and_5_out), .Sum(full_adder_1_sum), .Cout(full_adder_1_cout));
  full_adder full_adder_2 (
    .Cin(full_adder_1_cout), .A(and_6_out), .B(and_7_out), .Sum(full_adder_2_sum), .Cout(full_adder_2_cout));
  half_adder half_adder_2 (.A(full_adder_2_cout), .B(and_8_out), .Sum(half_adder_2_sum), .Cout(half_adder_2_cout));
  and and_9 (and_9_out, A[3], B[2]);
  and and_10 (and_10_out, A[0], B[2]);
  and and_11 (and_11_out, A[1], B[2]);
  and and_12 (and_12_out, A[2], B[2]);
  and and_13 (and_13_out, A[3], B[3]);
  half_adder half_adder_3 (.A(full_adder_1_sum), .B(and_10_out), .Sum(out_3[2]), .Cout(half_adder_3_cout));
  full_adder full_adder_3 (
    .Cin(half_adder_3_cout), .A(full_adder_2_sum), .B(and_11_out), .Sum(full_adder_3_sum),
    .Cout(full_adder_3_cout));
  full_adder full_adder_4 (
    .Cin(full_adder_3_cout), .A(half_adder_2_sum), .B(and_12_out), .Sum(full_adder_4_sum),
    .Cout(full_adder_4_cout));
  full_adder full_adder_5 (
    .Cin(full_adder_4_cout), .A(half_adder_2_cout), .B(and_9_out), .Sum(full_adder_5_sum),
    .Cout(full_adder_5_cout));
  and and_14 (and_14_out, A[0], B[3]);
  and and_15 (and_15_out, A[1], B[3]);
  and and_16 (and_16_out, A[2], B[3]);
  half_adder half_adder_4 (.A(full_adder_3_sum), .B(and_14_out), .Sum(out_3[3]), .Cout(half_adder_4_cout));
  full_adder full_adder_6 (
    .Cin(half_adder_4_cout), .A(full_adder_4_sum), .B(and_15_out), .Sum(out_3[4]), .Cout(full_adder_6_cout));
  full_adder full_adder_7 (
    .Cin(full_adder_6_cout), .A(full_adder_5_sum), .B(and_16_out), .Sum(out_3[5]), .Cout(full_adder_7_cout));
  full_adder full_adder_8 (
    .Cin(full_adder_7_cout), .A(full_adder_5_cout), .B(and_13_out), .Sum(out_3[6]), .Cout(out_3[7]));
endmodule

module full_adder (
  input  Cin,
  input  A,
  input  B,
  output Sum,
  output Cout
);

  wire and_1_out, and_2_out, xor_1_out;

  xor xor_1 (xor_1_out, Cin, A);
  xor xor_2 (Sum, xor_1_out, B);
  and and_1 (and_1_out, xor_1_out, B);
  and and_2 (and_2_out, Cin, A);
  or or_1 (Cout, and_1_out, and_2_out);
endmodule

module half_adder (
  input  A,
  input  B,
  output Sum,
  output Cout
);

  xor xor_1 (Sum, A, B);
  and and_1 (Cout, A, B);
endmodule
