// Logisim project 2-3.circ as structural Verilog: 2 circuits, main circuit mod_counter
module mod_counter (
  input  Switch,
  input  [3:0] N_minus_one
);

  wire and_1_out, Clk_out, Q0, Q1, Q2, Q3, t_ff_1_qn, t_ff_2_qn, t_ff_3_qn, xnor_1_out, xnor_2_out,
       xnor_3_out, xnor_4_out;

  T_Flip_Flop t_ff_1 (.T(Switch), .clk(Clk_out), .Q(Q0), .Qn(t_ff_1_qn), .reset(and_1_out));  // open: preset
  Clock Clk (.out(Clk_out));
  T_Flip_Flop t_ff_2 (.T(Switch), .clk(t_ff_1_qn), .Q(Q1), .Qn(t_ff_2_qn), .reset(and_1_out));  // open: preset
  xnor xnor_1 (xnor_1_out, Q0, N_minus_one[0]);
  xnor xnor_2 (xnor_2_out, Q1, N_minus_one[1]);
  xnor xnor_3 (xnor_3_out, Q2, N_minus_one[2]);
  and and_1 (and_1_out, xnor_1_out, xnor_2_out, xnor_3_out, xnor_4_out);
  T_Flip_Flop t_ff_3 (.T(Switch), .clk(t_ff_2_qn), .Q(Q2), .Qn(t_ff_3_qn), .reset(and_1_out));  // open: preset
  xnor xnor_4 (xnor_4_out, Q3, N_minus_one[3]);
  T_Flip_Flop t_ff_4 (.T(Switch), .clk(t_ff_3_qn), .Q(Q3), .reset(and_1_out));  // open: Qn, preset
  Hex_Digit_Display hex_digit_display_1 (.value({Q3, Q2, Q1, Q0}));  // open: dp
endmodule

module ten_counter (
  input  Switch
);

  wire and_1_out, Clk_out, Q0_qn, Q1_qn, Q2_qn;
  wire [3:0] Q0_q;

  T_Flip_Flop Q0 (.T(Switch), .clk(Clk_out), .Q(Q0_q[0]), .Qn(Q0_qn), .reset(and_1_out));  // open: preset
  Clock Clk (.out(Clk_out));
  T_Flip_Flop Q1 (.T(Switch), .clk(Q0_qn), .Q(Q0_q[1]), .Qn(Q1_qn), .reset(and_1_out));  // open: preset
  T_Flip_Flop Q2 (.T(Switch), .clk(Q1_qn), .Q(Q0_q[2]), .Qn(Q2_qn), .reset(and_1_out));  // open: preset
  T_Flip_Flop Q3 (.T(Switch), .clk(Q2_qn), .Q(Q0_q[3]), .reset(and_1_out));  // open: Qn, preset
  and and_1 (and_1_out, Q0_q[1], Q0_q[3]);
  Hex_Digit_Display hex_digit_display_1 (.value(Q0_q));  // open: dp
endmodule
