// Logisim project circuit.circ as structural Verilog: 1 circuit, main circuit main
module main (
  input  C,
  input  A0,
  input  B0,
  input  A1,
  input  B1,
  input  A2,
  input  B2,
  input  A3,
  input  B3,
  output S0,
  output S1,
  output S2,
  output S3,
  output P
);

  wire and_1_out, and_2_out, and_3_out, and_4_out, and_5_out, and_6_out, and_7_out, and_8_out, or_1_out,
       or_2_out, or_3_out, xor_1_out, xor_2_out, xor_3_out, xor_4_out;

  xor xor_1 (xor_1_out, A0, B0);
  xor xor_2 (xor_2_out, A1, B1);
  xor xor_3 (xor_3_out, A2, B2);
  and and_1 (and_1_out, B2, A2);
  xor xor_4 (xor_4_out, A3, B3);
  and and_2 (and_2_out, B3, A3);
  xor xor_5 (S0, xor_1_out, C);
  and and_3 (and_3_out, xor_1_out, C);
  and and_4 (and_4_out, B0, A0);
  and and_5 (and_5_out, B1, A1);
  or or_1 (or_1_out, and_6_out, and_1_out);
  or or_2 (or_2_out, and_7_out, and_5_out);
  and and_6 (and_6_out, or_2_out, xor_3_out);
  xor xor_6 (S3, or_1_out, xor_4_out);
  or or_3 (or_3_out, and_3_out, and_4_out);
  and and_7 (and_7_out, or_3_out, xor_2_out);
  and and_8 (and_8_out, or_1_out, xor_4_out);
  xor xor_7 (S1, or_3_out, xor_2_out);
  xor xor_8 (S2, or_2_out, xor_3_out);
  or or_4 (P, and_8_out, and_2_out);
endmodule
