// Logisim project circuit.circ as structural Verilog: 1 circuit, main circuit main
module main (
  input  x3,
  input  x2,
  input  x1,
  input  x0,
  input  y3,
  input  y2,
  input  y1,
  input  y0,
  output M,
  output R,
  output B
);

  wire and_1_out, and_2_out, and_3_out, and_4_out, and_5_out, and_6_out, and_7_out, and_8_out, and_9_out,
       and_10_out, and_11_out, not_1_out, not_2_out, not_3_out, not_4_out, not_5_out, not_6_out, not_7_out,
       not_8_out, not_9_out, not_10_out, not_11_out, not_13_out, or_1_out, or_2_out, or_3_out, or_4_out,
       or_5_out, or_6_out, or_7_out;

  not not_1 (not_1_out, x3);
  not not_2 (not_2_out, x2);
  not not_3 (not_3_out, x1);
  not not_4 (not_4_out, x0);
  not not_5 (not_5_out, y3);
  not not_6 (not_6_out, y2);
  not not_7 (not_7_out, y1);
  not not_8 (not_8_out, y0);
  and and_1 (and_1_out, not_2_out, y2);
  and and_2 (and_2_out, x1, not_7_out);
  and and_3 (and_3_out, not_3_out, y1);
  and and_4 (and_4_out, x0, not_8_out);
  and and_5 (and_5_out, not_4_out, y0);
  and and_6 (and_6_out, x3, not_5_out);
  and and_7 (and_7_out, not_1_out, y3);
  and and_8 (and_8_out, x2, not_6_out);
  or or_1 (or_1_out, and_2_out, and_3_out);
  or or_2 (or_2_out, and_4_out, and_5_out);
  or or_3 (or_3_out, and_6_out, and_7_out);
  or or_4 (or_4_out, and_8_out, and_1_out);
  not not_9 (not_9_out, or_1_out);
  not not_10 (not_10_out, or_4_out);
  and and_9 (and_9_out, not_9_out, and_4_out);
  not not_11 (not_11_out, or_3_out);
  or or_5 (or_5_out, or_3_out, or_4_out, or_1_out, or_2_out);
  or or_6 (or_6_out, and_9_out, and_2_out);
  and and_10 (and_10_out, not_10_out, or_6_out);
  not not_12 (R, or_5_out);
  or or_7 (or_7_out, and_8_out, and_10_out);
  and and_11 (and_11_out, not_11_out, or_7_out);
  or or_8 (B, and_6_out, and_11_out);
  and and_12 (M, or_5_out, not_13_out);
  not not_13 (not_13_out, B);
endmodule
