// Logisim project circuit.circ as structural Verilog: 3 circuits, main circuit main
module main (
  input  ADD,
  input  CLK,
  input  RES,
  output Q3,
  output Q2,
  output Q1,
  output Q0
);

  wire and_1_out, and_2_out;

  T_Flip_Flop T3 (.T(and_1_out), .clk(CLK), .Q(Q3), .reset(RES));  // open: Qn, preset
  and and_1 (and_1_out, Q2, Q1, Q0);
  T_Flip_Flop T2 (.T(and_2_out), .clk(CLK), .Q(Q2), .reset(RES));  // open: Qn, preset
  T_Flip_Flop T1 (.T(Q0), .clk(CLK), .Q(Q1), .reset(RES));  // open: Qn, preset
  and and_2 (and_2_out, Q1, Q0);
  T_Flip_Flop T0 (.T(ADD), .clk(CLK), .Q(Q0), .reset(RES));  // open: Qn, preset
endmodule

module async (
  input  CLR,
  input  CLK,
  output Q3,
  output Q2,
  output Q1,
  output Q0
);

  T_Flip_Flop #(.trigger("falling")) T3 (.T(1'b1), .clk(Q2), .Q(Q3), .reset(CLR));  // open: Qn, preset
  T_Flip_Flop #(.trigger("falling")) T2 (.T(1'b1), .clk(Q1), .Q(Q2), .reset(CLR));  // open: Qn, preset
  T_Flip_Flop #(.trigger("falling")) T1 (.T(1'b1), .clk(Q0), .Q(Q1), .reset(CLR));  // open: Qn, preset
  T_Flip_Flop #(.trigger("falling")) T0 (.T(1'b1), .clk(CLK), .Q(Q0), .reset(CLR));  // open: Qn, preset
endmodule

module ripple_sync (
  input  CLR,
  input  CLK,
  output Q3,
  output Q2,
  output Q1,
  output Q0
);

  wire and_1_out, and_2_out;

  T_Flip_Flop T3 (.T(and_1_out), .clk(CLK), .Q(Q3), .reset(CLR));  // open: Qn, preset
  and and_1 (and_1_out, and_2_out, Q2);
  T_Flip_Flop T2 (.T(and_2_out), .clk(CLK), .Q(Q2), .reset(CLR));  // open: Qn, preset
  T_Flip_Flop T1 (.T(Q0), .clk(CLK), .Q(Q1), .reset(CLR));  // open: Qn, preset
  and and_2 (and_2_out, Q1, Q0);
  T_Flip_Flop T0 (.T(1'b1), .clk(CLK), .Q(Q0), .reset(CLR));  // open: Qn, preset
endmodule
