// Logisim project circuit.circ as structural Verilog: 3 circuits, main circuit main
module main (
  input  CUP,
  input  WR,
  input  RES,
  input  D7,
  input  D6,
  input  D5,
  input  D4,
  input  D3,
  input  D2,
  input  D1,
  input  D0,
  output [7:0] Q
);

  wire compare_1_f, demultiplexer_1_out1, n7474_1_pin5, n74193_1_pin4, n74193_1_pin5, n74193_2_pin5,
       nand_1_out, not_1_out, not_2_out, not_3_out;

  not not_1 (not_1_out, RES);
  not not_2 (not_2_out, demultiplexer_1_out1);
  nand nand_1 (nand_1_out, not_1_out, not_2_out);
  _74193 u_74193_1 (
    .pin1(D5), .pin2(Q[5]), .pin3(Q[4]), .pin4(n74193_1_pin4), .pin5(n74193_1_pin5), .pin6(Q[6]),
    .pin7(Q[7]), .pin15(D4), .pin14(nand_1_out), .pin11(WR), .pin10(D6), .pin9(D7));  // open: pin13, pin12
  compare compare_1 (
    .A7(Q[7]), .A6(Q[6]), .A5(Q[5]), .A4(Q[4]), .A3(Q[3]), .A2(Q[2]), .A1(Q[1]), .A0(Q[0]), .F(compare_1_f));
  _74193 u_74193_2 (
    .pin1(D1), .pin2(Q[1]), .pin3(Q[0]), .pin4(n74193_1_pin4), .pin5(n74193_2_pin5), .pin6(Q[2]),
    .pin7(Q[3]), .pin15(D0), .pin14(nand_1_out), .pin12(n74193_1_pin5), .pin11(WR), .pin10(D2), .pin9(D3));  // open: pin13
  Demultiplexer demultiplexer_1 (.out0(n74193_2_pin5), .out1(demultiplexer_1_out1), .in(CUP), .sel(n7474_1_pin5));
  not not_3 (not_3_out, CUP);
  _7474 u_7474_1 (
    .pin5(n7474_1_pin5), .pin12(compare_1_f), .pin11(not_3_out));  // open: pin1, pin2, pin3, pin4, pin6, pin13, pin10, pin9, pin8
  // also tied to VCC on the sheet: n74193_1_pin4

  // Other names for the same wires on the sheet: L0 = Q[0]; L1 = Q[1]; L2 = Q[2]; L3 = Q[3]; L4 = Q[4]; L5 = Q[5];
  //   L6 = Q[6]; L7 = Q[7]
endmodule

module compare (
  input  A7,
  input  A6,
  input  A5,
  input  A4,
  input  A3,
  input  A2,
  input  A1,
  input  A0,
  output F
);

  wire nand_1_out, nand_2_out, nand_3_out, nand_4_out, nand_5_out, not_1_out, not_2_out, not_3_out,
       not_4_out, not_5_out, not_6_out, not_7_out;

  not not_1 (not_1_out, A7);
  not not_2 (not_2_out, A4);
  not not_3 (not_3_out, A3);
  nand nand_1 (nand_1_out, not_1_out, A6);
  nand nand_2 (nand_2_out, not_3_out, A2);
  not not_4 (not_4_out, nand_1_out);
  not not_5 (not_5_out, nand_2_out);
  nand nand_3 (nand_3_out, not_4_out, A5, not_2_out);
  not not_6 (not_6_out, nand_3_out);
  nand nand_4 (nand_4_out, not_5_out, A1, A0);
  not not_7 (not_7_out, nand_4_out);
  nand nand_5 (nand_5_out, not_6_out, not_7_out);
  not not_8 (F, nand_5_out);
endmodule

module cnt (
  input  in_1
);

  wire clock_1_out;
  wire [7:0] main_1_q;

  Clock clock_1 (.out(clock_1_out));
  main main_1 (.CUP(clock_1_out), .WR(in_1), .Q(main_1_q));  // open: RES, D7, D6, D5, D4, D3, D2, D1, D0
  Hex_Digit_Display hex_digit_display_1 (.value(main_1_q[7:4]));  // open: dp
  Hex_Digit_Display hex_digit_display_2 (.value(main_1_q[3:0]));  // open: dp
endmodule
