// Logisim project circuit.circ as structural Verilog: 3 circuits, main circuit main
module main (
  input  D,
  input  RES,
  output FF0,
  output FF1,
  output FF2,
  output out_6,
  output out_7,
  output out_8
);

  wire CLK_out;

  Clock CLK (.out(CLK_out));
  MasterSlave_D_Trigger masterslave_d_trigger_1 (
    .D1(D), .D0(CLK_out), .CLK(RES), .RES(RES), .Q0(FF0));  // open: Q1, N_Q1, N_Q0
  TTL_D_Trigger ttl_d_trigger_1 (.D(D), .CLK(CLK_out), .RES(RES), .Q(out_6));  // open: N_Q
  MasterSlave_D_Trigger masterslave_d_trigger_2 (
    .D1(FF0), .D0(CLK_out), .CLK(RES), .RES(RES), .Q0(FF1));  // open: Q1, N_Q1, N_Q0
  TTL_D_Trigger ttl_d_trigger_2 (.D(out_6), .CLK(CLK_out), .RES(RES), .Q(out_7));  // open: N_Q
  MasterSlave_D_Trigger masterslave_d_trigger_3 (
    .D1(FF1), .D0(CLK_out), .CLK(RES), .RES(RES), .Q0(FF2));  // open: Q1, N_Q1, N_Q0
  TTL_D_Trigger ttl_d_trigger_3 (.D(out_7), .CLK(CLK_out), .RES(RES), .Q(out_8));  // open: N_Q
endmodule

module MasterSlave_D_Trigger (
  input  D1,
  input  D0,
  input  CLK,
  input  RES,
  output Q0,
  output Q1,
  output N_Q1,
  output N_Q0
);

  wire nand_1_out, nand_2_out, nand_3_out, nand_4_out, nand_7_out, nand_8_out, nand_9_out, nand_10_out,
       not_1_out;

  not not_1 (not_1_out, RES);
  nand nand_1 (nand_1_out, nand_4_out, nand_2_out);
  nand nand_2 (nand_2_out, nand_1_out, CLK, not_1_out);
  nand nand_3 (nand_3_out, nand_2_out, CLK, nand_4_out);
  nand nand_4 (nand_4_out, nand_3_out, D0, not_1_out);
  nand nand_5 (Q0, nand_2_out, N_Q0);
  nand nand_6 (N_Q0, Q0, nand_3_out, not_1_out);
  nand nand_7 (nand_7_out, nand_10_out, nand_8_out);
  nand nand_8 (nand_8_out, nand_7_out, CLK, not_1_out);
  nand nand_9 (nand_9_out, nand_8_out, CLK, nand_10_out);
  nand nand_10 (nand_10_out, nand_9_out, D1, not_1_out);
  nand nand_11 (Q1, nand_8_out, N_Q1);
  nand nand_12 (N_Q1, Q1, nand_9_out, not_1_out);

  // Notes on the sheet:
  //   S
  //   R
  //   S
  //   R
endmodule

module TTL_D_Trigger (
  input  D,
  input  CLK,
  input  RES,
  output Q,
  output N_Q
);

  wire n7400_1_pin1, n7400_1_pin2, n7400_1_pin3, n7404_1_pin2, n7410_1_pin6;

  _7404 u_7404_1 (
    .pin1(RES), .pin2(n7404_1_pin2));  // open: pin3, pin4, pin5, pin6, pin13, pin12, pin11, pin10, pin9, pin8
  _7400 u_7400_1 (
    .pin1(n7400_1_pin1), .pin2(n7400_1_pin2), .pin3(n7400_1_pin3), .pin4(n7400_1_pin2), .pin5(N_Q), .pin6(Q));  // open: pin13, pin12, pin11, pin10, pin9, pin8
  _7410 u_7410_1 (
    .pin1(n7400_1_pin3), .pin2(CLK), .pin3(n7400_1_pin2), .pin4(CLK), .pin5(n7400_1_pin1),
    .pin6(n7410_1_pin6), .pin13(n7404_1_pin2), .pin12(n7400_1_pin2), .pin11(n7410_1_pin6), .pin10(D),
    .pin9(n7404_1_pin2), .pin8(n7400_1_pin1));
  _7410 u_7410_2 (
    .pin1(Q), .pin2(n7410_1_pin6), .pin13(n7404_1_pin2), .pin12(N_Q));  // open: pin3, pin4, pin5, pin6, pin11, pin10, pin9, pin8

  // Notes on the sheet:
  //   s
  //   r
endmodule
