// Logisim project circuit.circ as structural Verilog: 4 circuits, main circuit main
module main (
  input  I,
  input  RL,
  input  Set,
  input  Clr,
  input  WR,
  input  CLK,
  output Q1,
  output Q0,
  output N_Q1,
  output N_Q0
);

  wire and_1_out, and_2_out, and_3_out, and_4_out, and_5_out, and_6_out, and_7_out, and_8_out, and_9_out,
       and_10_out, and_11_out, and_12_out, nand_1_out, nand_2_out, nand_3_out, nand_4_out, nand_5_out,
       not_1_out, not_2_out, not_3_out, not_4_out, not_5_out, not_6_out, or_1_out, or_2_out;

  not not_1 (not_1_out, RL);
  and and_1 (and_1_out, I, RL);
  and and_2 (and_2_out, not_1_out, Q0);
  or or_1 (or_1_out, and_1_out, and_2_out);
  nor nor_1 (Q1, and_3_out, and_4_out);
  nand nand_1 (nand_1_out, WR, CLK);
  and and_3 (and_3_out, N_Q1, nand_2_out, Set);
  and and_4 (and_4_out, Set, not_2_out, N_Q1);
  nand nand_2 (nand_2_out, N_Q1, Clr, or_1_out, nand_1_out);
  not not_2 (not_2_out, nand_1_out);
  nand nand_3 (nand_3_out, Q1, Set, not_3_out, nand_1_out);
  and and_5 (and_5_out, Q1, nand_3_out, Clr);
  and and_6 (and_6_out, Clr, not_2_out, Q1);
  nor nor_2 (N_Q1, and_5_out, and_6_out);
  not not_3 (not_3_out, or_1_out);
  not not_4 (not_4_out, nand_1_out);
  and and_7 (and_7_out, Q1, RL);
  and and_8 (and_8_out, not_1_out, I);
  or or_2 (or_2_out, and_7_out, and_8_out);
  nor nor_3 (Q0, and_9_out, and_10_out);
  and and_9 (and_9_out, N_Q0, nand_4_out, Set);
  and and_10 (and_10_out, Set, not_5_out, N_Q0);
  nand nand_4 (nand_4_out, N_Q0, Clr, or_2_out, not_4_out);
  not not_5 (not_5_out, not_4_out);
  nand nand_5 (nand_5_out, Q0, Set, not_6_out, not_4_out);
  and and_11 (and_11_out, Q0, nand_5_out, Clr);
  and and_12 (and_12_out, Clr, not_5_out, Q0);
  nor nor_4 (N_Q0, and_11_out, and_12_out);
  not not_6 (not_6_out, or_2_out);

  // Notes on the sheet:
  //   2
  //   Q1
  //   J1
  //   2
  //   1
  //   1
  //   1
  //   2
  //   2
  //   1
  //   2
  //   1
  //   K1
  //   2
  //   1
  //   J0
  //   1
  //   1
  //   2
  //   2
  //   2
  //   1
  //   2
  //   K0
  //   1
endmodule

module right_one_ig (
  input  I,
  input  RL,
  input  Set,
  input  Clr,
  input  CLK,
  output Q1,
  output Q0,
  output N_Q1,
  output N_Q0
);

  wire and_1_out, and_2_out, and_3_out, and_4_out, and_5_out, and_6_out, and_7_out, and_8_out, and_9_out,
       and_10_out, and_11_out, and_12_out, nand_1_out, nand_2_out, nand_3_out, nand_4_out, not_1_out,
       not_2_out, not_3_out, not_4_out, not_5_out, not_6_out, or_1_out, or_2_out;

  not not_1 (not_1_out, RL);
  and and_1 (and_1_out, I, RL);
  and and_2 (and_2_out, not_1_out, Q0);
  or or_1 (or_1_out, and_1_out, and_2_out);
  nor nor_1 (Q1, and_3_out, and_4_out);
  and and_3 (and_3_out, N_Q1, nand_1_out, Set);
  and and_4 (and_4_out, Set, not_2_out, N_Q1);
  nand nand_1 (nand_1_out, N_Q1, Clr, or_1_out, CLK);
  not not_2 (not_2_out, CLK);
  nand nand_2 (nand_2_out, Q1, Set, not_3_out, CLK);
  and and_5 (and_5_out, Q1, nand_2_out, Clr);
  and and_6 (and_6_out, Clr, not_2_out, Q1);
  nor nor_2 (N_Q1, and_5_out, and_6_out);
  not not_3 (not_3_out, or_1_out);
  not not_4 (not_4_out, CLK);
  and and_7 (and_7_out, Q1, RL);
  and and_8 (and_8_out, not_1_out, I);
  or or_2 (or_2_out, and_7_out, and_8_out);
  nor nor_3 (Q0, and_9_out, and_10_out);
  and and_9 (and_9_out, N_Q0, nand_3_out, Set);
  and and_10 (and_10_out, Set, not_5_out, N_Q0);
  nand nand_3 (nand_3_out, N_Q0, Clr, or_2_out, not_4_out);
  not not_5 (not_5_out, not_4_out);
  nand nand_4 (nand_4_out, Q0, Set, not_6_out, not_4_out);
  and and_11 (and_11_out, Q0, nand_4_out, Clr);
  and and_12 (and_12_out, Clr, not_5_out, Q0);
  nor nor_4 (N_Q0, and_11_out, and_12_out);
  not not_6 (not_6_out, or_2_out);

  // Notes on the sheet:
  //   2
  //   Q1
  //   J1
  //   2
  //   1
  //   1
  //   1
  //   2
  //   2
  //   1
  //   2
  //   1
  //   K1
  //   2
  //   1
  //   J0
  //   1
  //   1
  //   2
  //   2
  //   2
  //   1
  //   2
  //   K0
  //   1
endmodule

module multiplexor (
  input  I0,
  input  I1,
  input  SI,
  output O0
);

  wire and_1_out, and_2_out, not_1_out;

  not not_1 (not_1_out, SI);
  and and_1 (and_1_out, I0, not_1_out);
  and and_2 (and_2_out, I1, SI);
  or or_1 (O0, and_1_out, and_2_out);
endmodule

module parzival (
  input  D,
  input  Res,
  output Q1,
  output Q0
);

  wire clock_1_out;

  D_Flip_Flop d_ff_1 (.D(D), .clk(clock_1_out), .Q(Q1), .reset(Res));  // open: Qn, preset
  Clock clock_1 (.out(clock_1_out));
  D_Flip_Flop d_ff_2 (.D(Q1), .clk(clock_1_out), .Q(Q0), .reset(Res));  // open: Qn, preset
endmodule
