// Logisim project test.circ as structural Verilog: 1 circuit, main circuit main
module main (
  input  S,
  input  CLR,
  input  J,
  input  K,
  input  CLK,
  output Q,
  output N_Q
);

  wire and_1_out, and_2_out, and_3_out, and_4_out, nand_1_out, nand_2_out, not_1_out;

  nor nor_1 (Q, and_1_out, and_2_out);
  and and_1 (and_1_out, N_Q, nand_1_out, S);
  and and_2 (and_2_out, S, not_1_out, N_Q);
  nand nand_1 (nand_1_out, N_Q, CLR, J, CLK);
  not not_1 (not_1_out, CLK);
  nand nand_2 (nand_2_out, Q, S, K, CLK);
  and and_3 (and_3_out, Q, nand_2_out, CLR);
  and and_4 (and_4_out, CLR, not_1_out, Q);
  nor nor_2 (N_Q, and_3_out, and_4_out);

  // Notes on the sheet:
  //   2
  //   1
  //   1
  //   1
  //   2
  //   2
  //   2
  //   1
  //   2
  //   1
endmodule
